# Fritzing sketch FrannieDescentFritzigDrawing (saved by Fritzing 0.9.3b)
breadboards: 1

parts:
  hc-sr1 = hc-sr04  # not connected
  J1 = Piezo Speaker
  Part1 = Arduino Mega 2560 (Rev3)
  R1 = Resistor [tolerance=±5% resistance=330 package=THT]
  R2 = Resistor [tolerance=±5% resistance=10k power=10k package=THT]
  S2 = Square Pushbutton
  LED1 = LED - 3mm [color="Red (660nm)" package="3 mm [THT]"]

nets:
  N1: J1.pin1, Part1.GND, R2.Pin_1, LED1.anode
  N2: Part1.5V, S2.leg1
  N3: Part1.D2_PWM, S2.leg0
  N4: Part1.D4_PWM, R1.Pin_1
  N5: R1.Pin_0, LED1.cathode

notes:
  [write your here]
