# Fritzing sketch Structure Drawing (saved by Fritzing 0.9.3b)
breadboards: 1

parts:
  R1 = Resistor [tolerance=±5% resistance=220 package=THT]
  R2 = Resistor [tolerance=±5% resistance=220 package=THT]
  Part1 = Arduino Uno (Rev3)
  VCC1 = Battery  # not connected
  J1 = Piezo Speaker
  S1 = Square Pushbutton
  U1 = MPL3115A2 [package=lga8]
  LED2 = LEDs [package=led10mm]

nets:
  N1: R1.Pin_0, S1.leg1
  GND: R1.Pin_1, R2.Pin_1, Part1.GND, J1.pin1, U1.GND, LED2.C, LED2.A
  N2: R2.Pin_0, Part1.D4
  N3: Part1.A4/SDA, U1.VDD
  N4: Part1.A5/SCL, U1.CAP
  N5: Part1.D5_PWM, J1.pin2
  N6: Part1.5V, S1.leg0, U1.VDDIO
